// Logisim project CPU.circ as structural Verilog: 7 circuits, main circuit GRF
module main (
  input  in_1,
  output [31:0] out_2,
  output out_3,
  output [4:0] out_4,
  output [31:0] out_5,
  output out_6,
  output [4:0] out_7,
  output [31:0] out_8
);

  wire alu_1_zero, clock_1_out, controller_1_alusrc, controller_1_mem2reg, controller_1_npc_sel,
       controller_1_regdst;
  wire [1:0] controller_1_aluctr, controller_1_extop;
  wire [26:0] alu_1_datao;
  wire [31:0] ext_1_imm32, grf_1_busa, multiplexer_2_out, ram_1_data;

  Clock clock_1 (.out(clock_1_out));
  IFU ifu_1 (
    .Reset(in_1), .Instr(out_2), .nPC_sel(controller_1_npc_sel), .in_5(clock_1_out), .Imm32(ext_1_imm32),
    .zero(alu_1_zero));
  // Probe on out_2[25:21]
  // Probe on out_2[20:16]
  // Probe on out_2[15:11]
  Controller controller_1 (
    .Op(out_2[31:26]), .\function (out_2[5:0]), .RegDst(controller_1_regdst), .ALUSrc(controller_1_alusrc),
    .Mem2Reg(controller_1_mem2reg), .RegWrite(out_3), .MemWrite(out_6), .nPC_Sel(controller_1_npc_sel),
    .ExtOp(controller_1_extop), .ALUctr(controller_1_aluctr));
  Multiplexer #(.width(5)) multiplexer_1 (
    .in0(out_2[20:16]), .in1(out_2[15:11]), .out(out_4), .sel(controller_1_regdst));  // open: en
  EXT ext_1 (.imm16(out_2[15:0]), .ExtOp(controller_1_extop), .imm32(ext_1_imm32));
  GRF grf_1 (
    .RA(out_2[25:21]), .RB(out_2[20:16]), .RW(out_4), .BusA(grf_1_busa), .BusB(out_8), .RegWrite(out_3),
    .BusW(out_5), .Clock(clock_1_out), .in_7(in_1));
  Multiplexer #(.width(32)) multiplexer_2 (
    .in0(out_8), .in1(ext_1_imm32), .out(multiplexer_2_out), .sel(controller_1_alusrc));  // open: en
  ALU alu_1 (
    .DataA(grf_1_busa), .DataB(multiplexer_2_out), .zero(alu_1_zero),
    .DataO({alu_1_datao[26:2], out_7, alu_1_datao[1:0]}), .ALUop(controller_1_aluctr));
  // Probe on {alu_1_datao[26:2], out_7, alu_1_datao[1:0]}
  // Probe on out_7
  Multiplexer #(.width(32)) multiplexer_3 (
    .in0({alu_1_datao[26:2], out_7, alu_1_datao[1:0]}), .in1(ram_1_data), .out(out_5),
    .sel(controller_1_mem2reg));  // open: en
  RAM #(.addrWidth(5), .dataWidth(32), .bus("separate")) ram_1 (
    .addr(out_7), .din(out_8), .data(ram_1_data), .str(out_6), .clk(clock_1_out), .clr(in_1));  // open: sel, ld
  // Probe on out_5

  // Other names for the same wires on the sheet: Instr[31:0] = out_2; MemAddr[4:0] = out_7; MemData[31:0] = out_8;
  //   MemWrite = out_6; RegAddr[4:0] = out_4; RegData[31:0] = out_5; RegWrite = out_3; Reset = in_1
endmodule

// Ctrl
module Controller (
  input  [5:0] Op,
  input  [5:0] \function ,
  output RegDst,
  output ALUSrc,
  output Mem2Reg,
  output RegWrite,
  output MemWrite,
  output nPC_Sel,
  output [1:0] ExtOp,
  output [1:0] ALUctr
);

  wire ADD_out, aluctr_rtype_1_add, aluctr_rtype_1_nop, aluctr_rtype_1_slt, aluctr_rtype_1_sub, beq_out,
       lui_out, lw_out, not_1_out, not_2_out, not_3_out, not_4_out, not_5_out, not_6_out, OR_out, ori_out,
       Rtype_out, SLT_out, SUB_out, sw_out;

  not not_1 (not_1_out, Op[4]);
  not not_2 (not_2_out, Op[5]);
  not not_3 (not_3_out, Op[3]);
  not not_4 (not_4_out, Op[2]);
  not not_5 (not_5_out, Op[1]);
  not not_6 (not_6_out, Op[0]);
  and Rtype (Rtype_out, not_2_out, not_1_out, not_3_out, not_4_out, not_5_out, not_6_out);
  and ori (ori_out, not_2_out, not_1_out, Op[3], Op[2], not_5_out, Op[0]);
  and lw (lw_out, Op[5], not_1_out, not_3_out, not_4_out, Op[1], Op[0]);
  and sw (sw_out, Op[5], not_1_out, Op[3], not_4_out, Op[1], Op[0]);
  and beq (beq_out, not_2_out, not_1_out, not_3_out, Op[2], not_5_out, not_6_out);
  and lui (lui_out, not_2_out, not_1_out, Op[3], Op[2], Op[1], Op[0]);
  buf u_RegDst (RegDst, Rtype_out);  // OR_Gate
  or u_ALUSrc (ALUSrc, ori_out, lw_out, sw_out, lui_out);
  buf u_Mem2Reg (Mem2Reg, lw_out);  // OR_Gate
  buf u_MemWrite (MemWrite, sw_out);  // OR_Gate
  or u_RegWrite (RegWrite, Rtype_out, ori_out, lw_out, lui_out);
  buf u_nPC_Sel (nPC_Sel, beq_out);  // OR_Gate
  buf ExtOp1 (ExtOp[1], lui_out);  // OR_Gate
  or ExtOp0 (ExtOp[0], lw_out, sw_out, beq_out);
  ALUctr_Rtype aluctr_rtype_1 (
    .\function (\function ), .Rtype(Rtype_out), .add(aluctr_rtype_1_add), .sub(aluctr_rtype_1_sub),
    .nop(aluctr_rtype_1_nop), .slt(aluctr_rtype_1_slt));
  or ADD (ADD_out, lw_out, sw_out, aluctr_rtype_1_add, aluctr_rtype_1_nop);
  or SUB (SUB_out, beq_out, aluctr_rtype_1_sub);
  or OR (OR_out, ori_out, lui_out);
  buf SLT (SLT_out, aluctr_rtype_1_slt);  // OR_Gate
  Priority_Encoder #(.select(2)) priority_encoder_1 (
    .in0(ADD_out), .in1(SUB_out), .in2(OR_out), .in3(SLT_out), .out(ALUctr));  // open: gs, en_out, en_in
endmodule

module IFU (
  input  nPC_sel,
  input  zero,
  input  Reset,
  input  [31:0] Imm32,
  input  in_5,
  output [31:0] Instr
);

  wire and_1_out;
  wire [31:0] adder_1_out, adder_2_out, multiplexer_1_out, register_1_q, shifter_1_out;

  and and_1 (and_1_out, nPC_sel, zero);
  Multiplexer #(.width(32)) multiplexer_1 (
    .in0(adder_1_out), .in1(adder_2_out), .out(multiplexer_1_out), .sel(and_1_out));  // open: en
  Register #(.width(32)) register_1 (.D(multiplexer_1_out), .Q(register_1_q), .clk(in_5), .clr(Reset));  // open: en
  Adder #(.width(32)) adder_1 (.a(32'h4), .b(register_1_q), .out(adder_1_out));  // open: cin, cout
  ROM #(.addrWidth(5), .dataWidth(32)) rom_1 (.addr(register_1_q[6:2]), .data(Instr));  // open: sel
  Shifter #(.width(32)) shifter_1 (.in(Imm32), .\dist (5'b00010), .out(shifter_1_out));
  Adder #(.width(32)) adder_2 (.a(shifter_1_out), .b(adder_1_out), .out(adder_2_out));  // open: cin, cout

  // Notes on the sheet:
  //   contents of rom_1 (hex, n*v repeats v):
  //   0 3c080001 35080001 1084821 1284823 0 0 0 11290000 ac090000 8c0a0000 1000ffff
endmodule

module GRF (
  input  [4:0] RA,
  input  [4:0] RB,
  input  RegWrite,
  input  [4:0] RW,
  input  [31:0] BusW,
  input  Clock,
  input  in_7,
  output [31:0] BusA,
  output [31:0] BusB
);

  wire demultiplexer_1_out1, demultiplexer_1_out2, demultiplexer_1_out3, demultiplexer_1_out4,
       demultiplexer_1_out5, demultiplexer_1_out6, demultiplexer_1_out7, demultiplexer_1_out8,
       demultiplexer_1_out9, demultiplexer_1_out10, demultiplexer_1_out11, demultiplexer_1_out12,
       demultiplexer_1_out13, demultiplexer_1_out14, demultiplexer_1_out15, demultiplexer_1_out16,
       demultiplexer_1_out17, demultiplexer_1_out18, demultiplexer_1_out19, demultiplexer_1_out20,
       demultiplexer_1_out21, demultiplexer_1_out22, demultiplexer_1_out23, demultiplexer_1_out24,
       demultiplexer_1_out25, demultiplexer_1_out26, demultiplexer_1_out27, demultiplexer_1_out28,
       demultiplexer_1_out29, demultiplexer_1_out30, demultiplexer_1_out31;
  wire [31:0] register_1_q, register_2_q, register_3_q, register_4_q, register_5_q, register_6_q,
       register_7_q, register_8_q, register_9_q, register_10_q, register_11_q, register_12_q, register_13_q,
       register_14_q, register_15_q, register_16_q, register_17_q, register_18_q, register_19_q,
       register_20_q, register_21_q, register_22_q, register_23_q, register_24_q, register_25_q,
       register_26_q, register_27_q, register_28_q, register_29_q, register_30_q, register_31_q;

  Demultiplexer #(.select(5)) demultiplexer_1 (
    .out1(demultiplexer_1_out1), .out2(demultiplexer_1_out2), .out3(demultiplexer_1_out3),
    .out4(demultiplexer_1_out4), .out5(demultiplexer_1_out5), .out6(demultiplexer_1_out6),
    .out7(demultiplexer_1_out7), .out8(demultiplexer_1_out8), .out9(demultiplexer_1_out9),
    .out10(demultiplexer_1_out10), .out11(demultiplexer_1_out11), .out12(demultiplexer_1_out12),
    .out13(demultiplexer_1_out13), .out14(demultiplexer_1_out14), .out15(demultiplexer_1_out15),
    .out16(demultiplexer_1_out16), .out17(demultiplexer_1_out17), .out18(demultiplexer_1_out18),
    .out19(demultiplexer_1_out19), .out20(demultiplexer_1_out20), .out21(demultiplexer_1_out21),
    .out22(demultiplexer_1_out22), .out23(demultiplexer_1_out23), .out24(demultiplexer_1_out24),
    .out25(demultiplexer_1_out25), .out26(demultiplexer_1_out26), .out27(demultiplexer_1_out27),
    .out28(demultiplexer_1_out28), .out29(demultiplexer_1_out29), .out30(demultiplexer_1_out30),
    .out31(demultiplexer_1_out31), .in(RegWrite), .sel(RW));  // open: out0, en
  Register #(.width(32)) register_1 (.D(BusW), .en(demultiplexer_1_out1), .Q(register_1_q), .clk(Clock), .clr(in_7));
  Register #(.width(32)) register_2 (.D(BusW), .en(demultiplexer_1_out2), .Q(register_2_q), .clk(Clock), .clr(in_7));
  Register #(.width(32)) register_3 (.D(BusW), .en(demultiplexer_1_out3), .Q(register_3_q), .clk(Clock), .clr(in_7));
  Register #(.width(32)) register_4 (.D(BusW), .en(demultiplexer_1_out4), .Q(register_4_q), .clk(Clock), .clr(in_7));
  Register #(.width(32)) register_5 (.D(BusW), .en(demultiplexer_1_out5), .Q(register_5_q), .clk(Clock), .clr(in_7));
  Register #(.width(32)) register_6 (.D(BusW), .en(demultiplexer_1_out6), .Q(register_6_q), .clk(Clock), .clr(in_7));
  Register #(.width(32)) register_7 (.D(BusW), .en(demultiplexer_1_out7), .Q(register_7_q), .clk(Clock), .clr(in_7));
  Register #(.width(32)) register_8 (.D(BusW), .en(demultiplexer_1_out8), .Q(register_8_q), .clk(Clock), .clr(in_7));
  Register #(.width(32)) register_9 (.D(BusW), .en(demultiplexer_1_out9), .Q(register_9_q), .clk(Clock), .clr(in_7));
  Register #(.width(32)) register_10 (.D(BusW), .en(demultiplexer_1_out10), .Q(register_10_q), .clk(Clock), .clr(in_7));
  Register #(.width(32)) register_11 (.D(BusW), .en(demultiplexer_1_out11), .Q(register_11_q), .clk(Clock), .clr(in_7));
  Register #(.width(32)) register_12 (.D(BusW), .en(demultiplexer_1_out12), .Q(register_12_q), .clk(Clock), .clr(in_7));
  Register #(.width(32)) register_13 (.D(BusW), .en(demultiplexer_1_out13), .Q(register_13_q), .clk(Clock), .clr(in_7));
  Register #(.width(32)) register_14 (.D(BusW), .en(demultiplexer_1_out14), .Q(register_14_q), .clk(Clock), .clr(in_7));
  Register #(.width(32)) register_15 (.D(BusW), .en(demultiplexer_1_out15), .Q(register_15_q), .clk(Clock), .clr(in_7));
  Register #(.width(32)) register_16 (.D(BusW), .en(demultiplexer_1_out16), .Q(register_16_q), .clk(Clock), .clr(in_7));
  Register #(.width(32)) register_17 (.D(BusW), .en(demultiplexer_1_out17), .Q(register_17_q), .clk(Clock), .clr(in_7));
  Register #(.width(32)) register_18 (.D(BusW), .en(demultiplexer_1_out18), .Q(register_18_q), .clk(Clock), .clr(in_7));
  Register #(.width(32)) register_19 (.D(BusW), .en(demultiplexer_1_out19), .Q(register_19_q), .clk(Clock), .clr(in_7));
  Register #(.width(32)) register_20 (.D(BusW), .en(demultiplexer_1_out20), .Q(register_20_q), .clk(Clock), .clr(in_7));
  Register #(.width(32)) register_21 (.D(BusW), .en(demultiplexer_1_out21), .Q(register_21_q), .clk(Clock), .clr(in_7));
  Register #(.width(32)) register_22 (.D(BusW), .en(demultiplexer_1_out22), .Q(register_22_q), .clk(Clock), .clr(in_7));
  Register #(.width(32)) register_23 (.D(BusW), .en(demultiplexer_1_out23), .Q(register_23_q), .clk(Clock), .clr(in_7));
  Register #(.width(32)) register_24 (.D(BusW), .en(demultiplexer_1_out24), .Q(register_24_q), .clk(Clock), .clr(in_7));
  Register #(.width(32)) register_25 (.D(BusW), .en(demultiplexer_1_out25), .Q(register_25_q), .clk(Clock), .clr(in_7));
  Register #(.width(32)) register_26 (.D(BusW), .en(demultiplexer_1_out26), .Q(register_26_q), .clk(Clock), .clr(in_7));
  Register #(.width(32)) register_27 (.D(BusW), .en(demultiplexer_1_out27), .Q(register_27_q), .clk(Clock), .clr(in_7));
  Register #(.width(32)) register_28 (.D(BusW), .en(demultiplexer_1_out28), .Q(register_28_q), .clk(Clock), .clr(in_7));
  Register #(.width(32)) register_29 (.D(BusW), .en(demultiplexer_1_out29), .Q(register_29_q), .clk(Clock), .clr(in_7));
  Register #(.width(32)) register_30 (.D(BusW), .en(demultiplexer_1_out30), .Q(register_30_q), .clk(Clock), .clr(in_7));
  Register #(.width(32)) register_31 (.D(BusW), .en(demultiplexer_1_out31), .Q(register_31_q), .clk(Clock), .clr(in_7));
  Multiplexer #(.select(5), .width(32)) multiplexer_1 (
    .in0({32{1'b0}}), .in1(register_1_q), .in2(register_2_q), .in3(register_3_q), .in4(register_4_q),
    .in5(register_5_q), .in6(register_6_q), .in7(register_7_q), .in8(register_8_q), .in9(register_9_q),
    .in10(register_10_q), .in11(register_11_q), .in12(register_12_q), .in13(register_13_q),
    .in14(register_14_q), .in15(register_15_q), .in16(register_16_q), .in17(register_17_q),
    .in18(register_18_q), .in19(register_19_q), .in20(register_20_q), .in21(register_21_q),
    .in22(register_22_q), .in23(register_23_q), .in24(register_24_q), .in25(register_25_q),
    .in26(register_26_q), .in27(register_27_q), .in28(register_28_q), .in29(register_29_q),
    .in30(register_30_q), .in31(register_31_q), .out(BusA), .sel(RA));  // open: en
  Multiplexer #(.select(5), .width(32)) multiplexer_2 (
    .in0({32{1'b0}}), .in1(register_1_q), .in2(register_2_q), .in3(register_3_q), .in4(register_4_q),
    .in5(register_5_q), .in6(register_6_q), .in7(register_7_q), .in8(register_8_q), .in9(register_9_q),
    .in10(register_10_q), .in11(register_11_q), .in12(register_12_q), .in13(register_13_q),
    .in14(register_14_q), .in15(register_15_q), .in16(register_16_q), .in17(register_17_q),
    .in18(register_18_q), .in19(register_19_q), .in20(register_20_q), .in21(register_21_q),
    .in22(register_22_q), .in23(register_23_q), .in24(register_24_q), .in25(register_25_q),
    .in26(register_26_q), .in27(register_27_q), .in28(register_28_q), .in29(register_29_q),
    .in30(register_30_q), .in31(register_31_q), .out(BusB), .sel(RB));  // open: en
endmodule

module ALU (
  input  [31:0] DataA,
  input  [31:0] DataB,
  input  [1:0] ALUop,
  output zero,
  output [31:0] DataO
);

  wire comparator_1_lt, or_2_out;
  wire [31:0] adder_1_out, bit_extender_1_out, or_1_out, subtractor_1_out;

  Adder #(.width(32)) adder_1 (.a(DataA), .b(DataB), .out(adder_1_out));  // open: cin, cout
  Subtractor #(.width(32)) subtractor_1 (.a(DataA), .b(DataB), .out(subtractor_1_out));  // open: bin, bout
  assign or_1_out = DataA | DataB;  // OR_Gate or_1, 32 bits wide
  Comparator #(.width(32)) comparator_1 (.a(DataA), .b(DataB), .lt(comparator_1_lt));  // open: gt, eq
  assign bit_extender_1_out = {{31{1'b0}}, comparator_1_lt};  // Bit_Extender bit_extender_1
  or or_2 (or_2_out, subtractor_1_out[15], subtractor_1_out[0], subtractor_1_out[1], subtractor_1_out[2], subtractor_1_out[3], subtractor_1_out[4], subtractor_1_out[5], subtractor_1_out[6], subtractor_1_out[7], subtractor_1_out[8], subtractor_1_out[9], subtractor_1_out[10], subtractor_1_out[11], subtractor_1_out[12], subtractor_1_out[13], subtractor_1_out[14], subtractor_1_out[16], subtractor_1_out[17], subtractor_1_out[18], subtractor_1_out[19], subtractor_1_out[20], subtractor_1_out[21], subtractor_1_out[22], subtractor_1_out[23], subtractor_1_out[24], subtractor_1_out[25], subtractor_1_out[26], subtractor_1_out[27], subtractor_1_out[28], subtractor_1_out[29], subtractor_1_out[30], subtractor_1_out[31]);
  Multiplexer #(.select(2), .width(32)) multiplexer_1 (
    .in0(adder_1_out), .in1(subtractor_1_out), .in2(or_1_out), .in3(bit_extender_1_out), .out(DataO),
    .sel(ALUop));  // open: en
  not not_1 (zero, or_2_out);
endmodule

// Ex
module EXT (
  input  [1:0] ExtOp,
  input  [15:0] imm16,
  output [31:0] imm32
);

  wire [31:0] bit_extender_1_out, bit_extender_2_out;

  assign bit_extender_1_out = {{16{1'b0}}, imm16};  // Bit_Extender bit_extender_1
  assign bit_extender_2_out = {{16{imm16[15]}}, imm16};  // Bit_Extender bit_extender_2
  Multiplexer #(.select(2), .width(32)) multiplexer_1 (
    .in0(bit_extender_1_out), .in1(bit_extender_2_out), .in2({imm16, {16{1'b0}}}), .out(imm32), .sel(ExtOp));  // open: in3, en
endmodule

module ALUctr_Rtype (
  input  [5:0] \function ,
  input  Rtype,
  output add,
  output sub,
  output nop,
  output slt
);

  wire not_1_out, not_2_out, not_3_out, not_4_out, not_5_out, not_6_out;

  not not_1 (not_1_out, \function [5]);
  not not_2 (not_2_out, \function [4]);
  not not_3 (not_3_out, \function [3]);
  not not_4 (not_4_out, \function [2]);
  not not_5 (not_5_out, \function [1]);
  not not_6 (not_6_out, \function [0]);
  and u_ADD (add, \function [5], not_2_out, not_3_out, not_4_out, not_5_out, \function [0], Rtype);
  and u_SUB (sub, \function [5], not_2_out, not_3_out, not_4_out, \function [1], \function [0], Rtype);
  and u_NOP (nop, not_1_out, not_2_out, not_3_out, not_4_out, not_5_out, not_6_out, Rtype);
  and u_SLT (slt, \function [5], not_2_out, \function [3], not_4_out, \function [1], not_6_out);
endmodule
